// Logisim project mupc.circ as structural Verilog
module main (
);

  wire CLOCK, demultiplexer_2_out0, demultiplexer_2_out1, demultiplexer_2_out2, demultiplexer_2_out3,
       multiplexer_3_out, REG_WRITE, RESET;
  wire [1:0] R1_SEL, R2_SEL, REG_SELECT;
  wire [3:0] OPCODE;
  wire [7:0] demultiplexer_1_out0, demultiplexer_1_out1, demultiplexer_1_out2, demultiplexer_1_out3, REG_1,
       REG_2, REG_A, REG_B, REG_IN, undriven;
  wire [15:0] REG_ADDRESS;

  Demultiplexer #(.select(2), .width(8)) demultiplexer_1 (
    .out0(demultiplexer_1_out0), .out1(demultiplexer_1_out1), .out2(demultiplexer_1_out2),
    .out3(demultiplexer_1_out3), .in(REG_IN), .sel(REG_SELECT));
  Demultiplexer #(.select(2)) demultiplexer_2 (
    .out0(demultiplexer_2_out0), .out1(demultiplexer_2_out1), .out2(demultiplexer_2_out2),
    .out3(demultiplexer_2_out3), .in(REG_WRITE), .sel(REG_SELECT));
  Multiplexer #(.select(2), .width(8)) multiplexer_1 (
    .in0(REG_A), .in1(REG_B), .in2(REG_ADDRESS[7:0]), .in3(REG_ADDRESS[15:8]), .out(REG_1), .sel(R1_SEL));
  Multiplexer #(.select(2), .width(8)) multiplexer_2 (
    .in0(REG_A), .in1(REG_B), .in2(REG_ADDRESS[7:0]), .in3(REG_ADDRESS[15:8]), .out(REG_2), .sel(R2_SEL));
  Register register_1 (.D(demultiplexer_1_out0), .en(demultiplexer_2_out0), .clk(CLOCK), .Q(REG_A), .clr(RESET));
  Register register_2 (.D(demultiplexer_1_out1), .en(demultiplexer_2_out1), .clk(CLOCK), .Q(REG_B), .clr(RESET));
  Register register_3 (
    .D(demultiplexer_1_out2), .en(demultiplexer_2_out2), .clk(CLOCK), .Q(REG_ADDRESS[7:0]), .clr(RESET));
  Register register_4 (
    .D(demultiplexer_1_out3), .en(demultiplexer_2_out3), .clk(CLOCK), .Q(REG_ADDRESS[15:8]), .clr(RESET));
  Multiplexer #(.select(4)) multiplexer_3 (
    .in0(1'b0), .in1(1'b0), .in2(1'b0), .in3(1'b0), .in4(1'b0), .in5(1'b0), .in6(1'b0), .in7(1'b0),
    .in8(1'b0), .in9(1'b0), .in10(1'b0), .in11(1'b0), .in12(1'b0), .in13(1'b0), .in14(1'b0), .in15(1'b0),
    .out(multiplexer_3_out), .sel(OPCODE));
  Multiplexer #(.select(4)) multiplexer_4 (
    .in0(1'b1), .in1(1'b1), .in2(1'b1), .in3(1'b1), .in4(1'b1), .in5(1'b1), .in6(1'b1), .in7(1'b1),
    .in8(1'b0), .in9(1'b0), .in10(1'b0), .in11(1'b0), .in13(1'b1), .in14(1'b0), .in15(1'b1), .out(REG_WRITE),
    .sel(OPCODE));  // open: in12
  Multiplexer #(.width(2)) multiplexer_5 (.in0(R1_SEL), .in1(R2_SEL), .out(REG_SELECT), .sel(multiplexer_3_out));
  Multiplexer #(.select(4), .width(8)) multiplexer_6 (
    .in0(undriven), .out(REG_IN), .sel(OPCODE));  // open: in1, in2, in3, in4, in5, in6, in7, in8, in9, in10, in11, in12, in13, in14, in15

  // Other names for the same wires on the sheet: REG_C[7:0] = REG_ADDRESS[7:0]; REG_D[7:0] = REG_ADDRESS[15:8]
endmodule
